# Fritzing sketch wiring (saved by Fritzing 0.9.2b)

parts:
  Part1 = Arduino Ethernet Shield (Rev3)
  Part2 = Arduino Uno (Rev3)  # not connected
  R1 = Resistor [tolerance=±5% resistance=10k package=THT]
  DHT11 = DHT11 Humitidy and Temperature Sensor

nets:
  N1: Part1.D2, R1.Pin_0, DHT11.DATA
  5V: Part1.5V, R1.Pin_1, DHT11.VDD
  GND: Part1.GND, DHT11.GND

custom parts:
  DHT11 Humitidy and Temperature Sensor: DHT11 Humidity and Temperature Sensor
